// Digital circuit alu.dig as structural Verilog
module alu (
  input  [15:0] A,
  input  [15:0] B,
  input  [1:0] ALUOP,
  output [15:0] RESULT,
  output [3:0] FLAG
);

  wire add_1_c_o, xnor_1_out, xor_1_out;
  wire [15:0] add_1_s, and_1_out, multiplexer_1_out, not_1_out, or_1_out;

  assign not_1_out = ~B;  // Not not_1, 16 bits wide
  Multiplexer #(.Bits(16)) multiplexer_1 (.sel(ALUOP[0]), .in_0(B), .in_1(not_1_out), .out(multiplexer_1_out));
  Add #(.Bits(16)) add_1 (.a(A), .b(multiplexer_1_out), .c_i(ALUOP[0]), .s(add_1_s), .c_o(add_1_c_o));
  assign and_1_out = A & B;  // And and_1, 16 bits wide
  assign or_1_out = A | B;  // Or or_1, 16 bits wide
  and and_2 (FLAG[3], add_1_c_o, ALUOP[1]);
  xnor xnor_1 (xnor_1_out, A[15], multiplexer_1_out[15]);
  and and_3 (FLAG[2], xor_1_out, xnor_1_out, ALUOP[1]);
  xor xor_1 (xor_1_out, FLAG[1], A[15]);
  Multiplexer #(.Selector_Bits(2), .Bits(16)) multiplexer_2 (
    .sel(ALUOP), .in_0(and_1_out), .in_1(or_1_out), .in_2(add_1_s), .in_3(add_1_s),
    .out({FLAG[1], RESULT[14:0]}));
  nor nor_1 (FLAG[0], RESULT[0], RESULT[1], RESULT[2], RESULT[3], RESULT[4], RESULT[5], RESULT[6], RESULT[7], RESULT[8], RESULT[9], RESULT[10], RESULT[11], RESULT[12], RESULT[13], RESULT[14], FLAG[1]);

  assign RESULT[15] = FLAG[1];

  // Notes on the sheet:
  //   A: First input to ALU
  //   B: Second input to ALU
  //   ALUOP: Operation selection input
  //   RESULT: The result of this ALU operation
  //   FLAG: The flags associated with the result of this ALU operation
  //   0. Z (zero)
  //   1. N (negative)
  //   2. C (carry)
  //   3. V (overflow)
  //   C
  //   V
  //   N
  //   Z
endmodule
