// Digital circuit basic-cpu.dig as structural Verilog
module basic_cpu (
  input  CLK
);

  wire and_2_out, CU_exec, FLEN, ld, SETH, STR, WE;
  wire [1:0] ALUOP, DMUX;
  wire [2:0] RS1, RS2, WS;
  wire [3:0] alu_1_flag;
  wire [7:0] reg_file_1_out1;
  wire [15:0] alu_1_result, and_1_out, multiplexer_1_out, multiplexer_2_out, multiplexer_3_out,
       notconnected_1_out, RAM_d1, RAM_d2, reg_file_1_fl, reg_file_1_out2, reg_file_1_pc;
  wire [15:8] reg_file_1_out1_2;

  assign and_1_out = 16'hff & RAM_d2;  // And and_1, 16 bits wide
  Multiplexer #(.Selector_Bits(2), .Bits(16)) multiplexer_1 (
    .sel(DMUX), .in_0(notconnected_1_out), .in_1(alu_1_result), .in_2(multiplexer_3_out),
    .in_3(multiplexer_2_out), .out(multiplexer_1_out));
  // NotConnected on notconnected_1_out
  Multiplexer #(.Bits(16)) multiplexer_2 (
    .sel(SETH), .in_0(and_1_out), .in_1({RAM_d2[7:0], reg_file_1_out1}), .out(multiplexer_2_out));
  // Probe DATA on multiplexer_1_out
  and and_2 (and_2_out, RS1[0], RS1[1], RS1[2]);
  Multiplexer #(.Bits(16)) multiplexer_3 (
    .sel(and_2_out), .in_0(RAM_d1), .in_1(reg_file_1_fl), .out(multiplexer_3_out));
  control_unit CU (
    .INST(RAM_d2), .ZERO(reg_file_1_fl[0]), .ALUOP(ALUOP), .RS1(RS1), .RS2(RS2), .WS(WS), .STR(STR), .WE(WE),
    .DMUX(DMUX), .LDR(ld), .FLEN(FLEN), .EXEC(CU_exec), .SETH(SETH));
  LED led_1 (.in(CU_exec));
  reg_file reg_file_1 (
    .RS1(RS1), .RS2(RS2), .WE(WE), .IN(multiplexer_1_out), .clk(CLK), .WS(WS), .FLD(alu_1_flag), .FLEN(FLEN),
    .OUT1({reg_file_1_out1_2, reg_file_1_out1}), .OUT2(reg_file_1_out2), .PC(reg_file_1_pc),
    .FL(reg_file_1_fl));
  RAMDualAccess #(.AddrBits(16), .isProgramMemory("true"), .Bits(16)) RAM (
    .str(STR), .C(CLK), .ld(ld), .A1({reg_file_1_out1_2, reg_file_1_out1}), .Din1(reg_file_1_out2),
    .A2(reg_file_1_pc), .D1(RAM_d1), .D2(RAM_d2));
  alu alu_1 (
    .A({reg_file_1_out1_2, reg_file_1_out1}), .B(reg_file_1_out2), .ALUOP(ALUOP), .RESULT(alu_1_result),
    .FLAG(alu_1_flag));

  // Notes on the sheet:
  //   DMUX
  //   Check FL register
  //   INST
endmodule
