// Digital circuit extended-cpu.dig as structural Verilog
module extended_cpu (
  input  CLK
);

  wire ALUIM, and_1_out, CALL, CALREG, extended_cu_1_exec, extended_cu_1_setc, FLEN, ld, MEMIM,
       multiplexer_4_out, PSTO, SETH, STR, WE, WE2;
  wire [1:0] ALUOP, COND_q, DMUX;
  wire [2:0] multiplexer_5_out, R3, RS1, RS2, WS;
  wire [3:0] alu_1_flag;
  wire [7:0] extended_regfile_1_out1;
  wire [15:0] alu_1_result, extended_regfile_1_fl, extended_regfile_1_out2, extended_regfile_1_out3,
       extended_regfile_1_pc, extended_regfile_1_pc_plus_1, IMM, multiplexer_1_out, multiplexer_2_out,
       multiplexer_3_out, multiplexer_6_out, multiplexer_7_out, multiplexer_8_out, multiplexer_9_out,
       multiplexer_10_out, multiplexer_11_out, notconnected_1_out, RAM_d1, RAM_d2;
  wire [15:8] extended_regfile_1_out1_2;

  Multiplexer #(.Selector_Bits(2), .Bits(16)) multiplexer_1 (
    .sel(DMUX), .in_0(notconnected_1_out), .in_1(alu_1_result), .in_2(multiplexer_6_out),
    .in_3(multiplexer_2_out), .out(multiplexer_1_out));
  // NotConnected on notconnected_1_out
  Multiplexer #(.Bits(16)) multiplexer_2 (
    .sel(SETH), .in_0(multiplexer_3_out), .in_1({RAM_d2[7:0], extended_regfile_1_out1}),
    .out(multiplexer_2_out));
  Multiplexer #(.Bits(16)) multiplexer_3 (
    .sel(CALREG), .in_0(IMM), .in_1(extended_regfile_1_out3), .out(multiplexer_3_out));
  // Probe DATA on multiplexer_1_out
  extended_cu extended_cu_1 (
    .INST(RAM_d2), .COND(multiplexer_4_out), .RS1(RS1), .RS2(RS2), .WS(WS), .STR(STR), .WE(WE), .DMUX(DMUX),
    .LDR(ld), .SETH(SETH), .RS3(R3), .IMM(IMM), .PSTO(PSTO), .FLEN(FLEN), .ALUOP(ALUOP), .WE2(WE2),
    .MEMIM(MEMIM), .CALREG(CALREG), .CALL(CALL), .ALUIM(ALUIM), .EXEC(extended_cu_1_exec),
    .SETC(extended_cu_1_setc));
  LED led_1 (.in(extended_cu_1_exec));
  Register #(.Bits(2)) COND (.D(WS[1:0]), .C(CLK), .en(extended_cu_1_setc), .Q(COND_q));
  Multiplexer #(.Selector_Bits(2)) multiplexer_4 (
    .sel(COND_q), .in_0(extended_regfile_1_fl[0]), .in_1(extended_regfile_1_fl[1]),
    .in_2(extended_regfile_1_fl[2]), .in_3(extended_regfile_1_fl[3]), .out(multiplexer_4_out));
  Multiplexer #(.Bits(3)) multiplexer_5 (.sel(CALL), .in_0(RS1), .in_1(3'b110), .out(multiplexer_5_out));
  extended_regfile extended_regfile_1 (
    .RS1(RS1), .RS2(RS2), .WE1(WE), .IN1(multiplexer_1_out), .clk(CLK), .WS1(WS), .RS3(R3),
    .WS2(multiplexer_5_out), .IN2(alu_1_result), .PRI(1'b1), .WE2(WE2), .FLD(alu_1_flag), .FLEN(FLEN),
    .OUT1({extended_regfile_1_out1_2, extended_regfile_1_out1}), .OUT2(extended_regfile_1_out2),
    .PC(extended_regfile_1_pc), .OUT3(extended_regfile_1_out3), .PC_plus_1(extended_regfile_1_pc_plus_1),
    .FL(extended_regfile_1_fl));
  and and_1 (and_1_out, RS1[0], RS1[1], RS1[2], ~MEMIM);  // And
  Multiplexer #(.Bits(16)) multiplexer_6 (
    .sel(and_1_out), .in_0(RAM_d1), .in_1(extended_regfile_1_fl), .out(multiplexer_6_out));
  Multiplexer #(.Bits(16)) multiplexer_7 (
    .sel(CALL), .in_0(extended_regfile_1_out3), .in_1({16{1'b1}}), .out(multiplexer_7_out));
  Multiplexer #(.Bits(16)) multiplexer_8 (.sel(ALUIM), .in_0(multiplexer_7_out), .in_1(IMM), .out(multiplexer_8_out));
  alu alu_1 (
    .A({extended_regfile_1_out1_2, extended_regfile_1_out1}), .B(multiplexer_8_out), .ALUOP(ALUOP),
    .RESULT(alu_1_result), .FLAG(alu_1_flag));
  Multiplexer #(.Bits(16)) multiplexer_9 (.sel(MEMIM), .in_0(alu_1_result), .in_1(IMM), .out(multiplexer_9_out));
  Multiplexer #(.Bits(16)) multiplexer_10 (
    .sel(PSTO), .in_0(multiplexer_9_out), .in_1({extended_regfile_1_out1_2, extended_regfile_1_out1}),
    .out(multiplexer_10_out));
  Multiplexer #(.Bits(16)) multiplexer_11 (
    .sel(CALL), .in_0(extended_regfile_1_out2), .in_1(extended_regfile_1_pc_plus_1), .out(multiplexer_11_out));
  RAMDualAccess #(.AddrBits(16), .isProgramMemory("true"), .Bits(16)) RAM (
    .str(STR), .C(CLK), .ld(ld), .A1(multiplexer_10_out), .Din1(multiplexer_11_out),
    .A2(extended_regfile_1_pc), .D1(RAM_d1), .D2(RAM_d2));

  // Notes on the sheet:
  //   UNIT TESTS FOR EACH EXTENSION
  //   (Except Pre/Post LDR/STR, these tests
  //   are not converted to digital tests, but they
  //   can be found in the unit tests folder)
  //   Assembly tests converted to Digital
  //   Integration Tests
  //   DMUX
  //   Checks FL reg
  //   INST
  //   SETH Logic
  //   Address Bus
endmodule

/* Test case FIB_20:
# This test calculates the 20th fibonacci number
# which should be 6765 = 0x1A6D. Refer to fib.quac
# in the assignment repo for the assembly code.

	CLK	R4

loop(i, 226)
	c	x	#Don't care about intermediate steps
end loop

	c	6765	#Result of fibonacci number calculation

program(0x0000, 0x2201, 0x0114, 0x0000, 0x0000, 0x3101, 0x1014, 0x44AF, 0x0532, 0x0000, 0x43AF, 0x44AE, 0xA443, 0x7420, 0xB5E1, 0x0000, 0x0000, 0x0000, 0x0000, 0x0000, 0x90A1, 0xF101, 0xBDE1, 0x0301, 0x93A1, 0xF101, 0xBDE1, 0x030A, 0x3300, 0xE201, 0x0519, 0x0000)
*/

/* Test case ALUIM:
# This tests ALU immediate operations. R1 tests add, R2 tests sub, R3 tests AND, R4 tests ORR
# Assembly: unit_tests/aluim.quac
	CLK	R1	R2	R3	R4

loop(i, 55)
	c	x	x	x	x	#Don't care about intermediate steps
end loop

	c	(210)	(21)	(58)	(241)

program(0x0000, 0x0000, 0xE101, 0xE102, 0xE103, 0xE104, 0xE105, 0xE106, 0xE107, 0xE108, 0xE109, 0xE10A, 0xE10B, 0xE10C, 0xE10D, 0xE10E, 0xE10F, 0xE110, 0xE111, 0xE112, 0xE113, 0xE114, 0x02D2, 0xF214, 0xF213, 0xF212, 0xF211, 0xF210, 0xF20F, 0xF20E, 0xF20D, 0xF20C, 0xF20B, 0xF20A, 0xF209, 0xF208, 0xF207, 0x03FF, 0xC3FF, 0xC3FB, 0xC3BF, 0xC3BB, 0xC3FF, 0xC3FE, 0xC37F, 0x0000, 0xD400, 0xD401, 0xD481, 0xD410, 0xD420, 0xD401, 0xD440, 0x0000, 0x0000, 0x0000, 0x0000, 0x0000, 0x0000, 0x0000, 0x0000, 0x0000, 0x0000, 0x0000)
*/

/* Test case SETC:
# This tests SETC.
# Assembly: unit_tests/setc.quac
	CLK	R1	R2	R3	R4

loop(i, 30)
	c	x	x	x	x	#Don't care about intermediate steps
end loop
	c	(0)	(50)	(60)	(0)

program(0x0000, 0x3101, 0xE000, 0x09FF, 0xF005, 0x09FF, 0x3201, 0x0900, 0x3301, 0x0900, 0x3001, 0x0900, 0x3101, 0x0900, 0x3001, 0xE000, 0x09FF, 0x3301, 0x0101, 0x2141, 0xA111, 0x0100, 0x3001, 0x0A32, 0x3101, 0x0A32, 0x3201, 0x0B3C, 0x3301, 0x0A46, 0x0000, 0x0000)
*/

/* Test case FACTORIAL_7:
# This test calculates 7! = 5040.

	CLK	R4

loop(i, 5514)
	c	x	#Don't care about intermediate steps
end loop

	c	5040	#Result of factorial

program(0x0107, 0x61F0, 0x2210, 0x0301, 0x7320, 0x102D, 0x053B, 0x0000, 0x0000, 0x0000, 0x0000, 0x0000, 0x0000, 0x0000, 0x0000, 0x0400, 0x51F1, 0x53F2, 0xA010, 0x6CF3, 0xBDE1, 0xA443, 0xF101, 0xF505, 0x0000, 0x0000, 0x0000, 0x0000, 0x0000, 0x4120, 0x61F1, 0x0300, 0x2310, 0xB323, 0xE301, 0x63F2, 0x100F, 0x51F3, 0x81A1, 0xB5E1, 0x0000, 0x0000, 0x0000, 0x0000, 0x0000, 0x0100, 0x2110, 0xB121, 0x53F0, 0xB031, 0x4C20, 0x6CF4, 0xBDE1, 0x101D, 0xF509, 0x0000, 0x0000, 0x0000, 0x0000, 0x0000, 0x0000, 0x0000, 0x0000, 0x0000)
*/

/* Test case MEMIM:
# This tests memory immediate operations.
# Assembly: unit_tests/memim.quac
	CLK	R1	R2	R3	R4

loop(i, 16)
	c	x	x	x	x	#Don't care about intermediate steps
end loop

	c	(200)	(100)	(0xAD)	(0xDE)

program(0x0000, 0x0000, 0x0000, 0x01DE, 0x02AD, 0x61FE, 0x62FF, 0x53FF, 0x54FE, 0x0164, 0x02C8, 0x6101, 0x6202, 0x5201, 0x5102, 0x0000)
*/

/* Test case MULT_11x13 (Function Calls):
# This test multiplies 11 by 13 by repeated addition. 11 x 13 = 143,
# so the result of R4 at the end should be 143.

	CLK	R4

loop(i, 86)
	c	x	#Don't care about intermediate steps
end loop

	c	0x008F	#Result of multiplication

program(0x100B, 0x0515, 0xA442, 0xF301, 0xB5E1, 0x0000, 0x0000, 0x1002, 0xBDE1, 0x0507, 0x0000, 0x0000, 0x5213, 0x5314, 0x1006, 0xB5E1, 0x0000, 0x0000, 0x0000, 0x000B, 0x000D, 0x0200, 0x0000, 0x0000, 0x0000, 0x0000, 0x0000, 0x0000, 0x0000, 0x0000, 0x0000, 0x0000)
*/

/* Test case PUSH POP:
# This tests PUSH and POP operation.
# Assembly: unit_tests/stack.quac
	CLK	R1	R2	R3	R4

loop(i, 21)
	c	x	x	x	x	#Don't care about intermediate steps
end loop
	c	(0xE9)	(0xCA)	(0xAB)	(1)

program(0x0000, 0x0000, 0x0000, 0x0101, 0x02AB, 0x03DE, 0x0423, 0x81EF, 0x82EF, 0x83EF, 0x84EF, 0xB0E1, 0xB0E1, 0x01CA, 0x02E9, 0x81EF, 0x82EF, 0xB1E1, 0xB2E1, 0xB3E1, 0xB4E1, 0x0000, 0x0000, 0x0000, 0x0000, 0x0000, 0x0000, 0x0000, 0x0000, 0x0000, 0x0000, 0x0000)
*/

/* Test case BUBBLE SORT:
# This test uses a 64-bit key-value pair bubble sort algorithm where comparisons are made only on keys, and key-value relationship remains unchanged.
# For more information, see demo.quac.

	CLK	R2

loop(i, 598)
	c	x
end loop
	c	0x0003
	c	x
	c	0x0064
	c	x
	c	0x006E
	c	x
	c	0x0078
	c	x
	c	0x0028
	c	x
	c	0x0007
	c	x
	c	0x0008
	c	x
	c	0x0009
	c	x
	c	0x0032
	c	x
	c	0x0004
	c	x
	c	0x0005
	c	x
	c	0x0006
	c	x
	c	0x0082
	c	x
	c	0x0001
	c	x
	c	0x0002
	c	x
	c	0x0003
	c	x
	c	0x00C9
	c	x
	c	0x000A
	c	x
	c	0x000B
	c	x
	c	0x000C
	c	x


program(0x1011, 0x106E, 0x057A, 0x0000, 0x0000, 0x0000, 0x0000, 0x0000, 0x0000, 0x0000, 0x0100, 0x0200, 0x0300, 0x0400, 0xB5E1, 0x0000, 0x0000, 0x100A, 0x0000, 0x2103, 0x0000, 0x0282, 0x9294, 0x0232, 0x9294, 0x0228, 0x9294, 0x02C9, 0x9294, 0x0203, 0x9294, 0x0100, 0x2103, 0x0000, 0x0201, 0x0302, 0x0403, 0x8291, 0x8391, 0x8491, 0x0204, 0x0305, 0x0406, 0x8292, 0x8391, 0x8491, 0x0207, 0x0308, 0x0409, 0x8292, 0x8391, 0x8491, 0x020A, 0x030B, 0x040C, 0x8292, 0x8391, 0x8491, 0x0264, 0x036E, 0x0478, 0x8292, 0x8391, 0x8491, 0x0100, 0x2103, 0x61F2, 0x0210, 0xA112, 0x61F1, 0xB5E1, 0x0000, 0x0000, 0x3001, 0x51F2, 0x0200, 0x4312, 0xE104, 0x4412, 0x7312, 0xF104, 0x7412, 0xE201, 0x0304, 0xB023, 0xBDE1, 0xF50A, 0x0000, 0x0000, 0x0000, 0x0100, 0x2103, 0x61F2, 0x52F2, 0x51F1, 0x3001, 0xB012, 0xBDE1, 0x3101, 0x4320, 0x44A4, 0xB043, 0x1849, 0x3101, 0x52F2, 0xE204, 0x62F2, 0xF50D, 0x0000, 0x0000, 0x3001, 0x015A, 0x3100, 0x52F1, 0xF204, 0x62F1, 0x0300, 0x2303, 0xB023, 0xBDE1, 0xF509, 0x0000, 0x0100, 0x2103, 0x4210, 0xE101, 0x4210, 0xE101, 0x4210, 0xE101, 0x4210, 0xE101, 0x4210, 0xE101, 0x4210, 0xE101, 0x4210, 0xE101, 0x4210, 0xE101, 0x4210, 0xE101, 0x4210, 0xE101, 0x4210, 0xE101, 0x4210, 0xE101, 0x4210, 0xE101, 0x4210, 0xE101, 0x4210, 0xE101, 0x4210, 0xE101, 0x4210, 0xE101, 0x4210, 0xE101, 0x4210, 0xE101, 0x4210, 0xE101, 0x0000, 0x0000, 0x0000, 0x0000, 0x0000, 0x0000, 0x0000, 0x0000, 0x0000, 0x0000, 0x0000, 0x0000)
*/

/* Test case BASE-OFFSET:
# This tests base+offset immediate operations.
# Assembly: unit_tests/base_offset.quac
	CLK	R1	R2	R3	R4

loop(i, 24)
	c	x	x	x	x	#Don't care about intermediate steps
end loop

	c	(3)	x	(4)	(5)

loop(i, 21)
	c	x	x	x	x	
end loop
	c	(0)	(0x2B)	(7)	(0x1B)

program(0x0000, 0x0000, 0x0000, 0x0103, 0x02F0, 0x0300, 0x7123, 0x0301, 0x0104, 0x7123, 0x0302, 0x0105, 0x7123, 0x0303, 0x0106, 0x7123, 0x4124, 0x0401, 0x4324, 0x0402, 0x4424, 0x0000, 0x0000, 0x0000, 0x020B, 0x01E0, 0x729F, 0x021B, 0x7298, 0x022B, 0x7297, 0x023B, 0x7294, 0x0305, 0x7392, 0x0306, 0x739C, 0x0307, 0x739B, 0x0308, 0x7396, 0x4297, 0x439B, 0x4498, 0x4190, 0x0000, 0x0000, 0x0000)
*/
